# Fritzing sketch Ph_10 (saved by Fritzing 0.9.9b)
breadboards: 1

parts:
  L1 = Inductor [package="400 mil [THT]"]
  R1 = Resistor [tolerance=±5% power=0.25 resistance=220 package=THT]
  U = Battery Holders [package=battery-aa-panel]
  LED1 = LEDs [package=led10mm]
  R2 = Resistor [tolerance=±5% power=0.25 resistance=220 package=THT]
  S1 = SWITCH-MOMENTARY-2 [package=tactile-switch-1101ne]

nets:
  N1: L1.pin_0, U.-, LED1.A
  N2: L1.pin_1, R2.Pin_0
  N3: R1.Pin_0, LED1.C
  N4: R1.Pin_1, R2.Pin_1, S1.2
  N5: U.+, S1.1
